// Logisim project SAP_1.circ as structural Verilog
module main (
);

  wire [7:0] ram16x8_1_out_4;

  InputAndMAR inputandmar_1 ();  // open: n_Lm, CLK, in_2, out_4, out_5
  RAM16x8 ram16x8_1 (.out_4(ram16x8_1_out_4));  // open: n_CE, in_1, in_2
  InstructionRegister instructionregister_1 (.in_2(ram16x8_1_out_4));  // open: Li, CLK, CLR, n_Ei, out_7, out_6
  Controller controller_1 ();  // open: in_1, out_6, CLK, nCLK, CLR, nCLR
  ProgramCounter programcounter_1 ();  // open: Cp, n_CLK, n_CLR, Ep, out_5
  OutputRegister outputregister_1 ();
  AccumulatorA accumulatora_1 ();  // open: in_2, n_La, CLK, Ea, out_5, out_6
  AdderSubtractor addersubtractor_1 ();  // open: in_1, in_4, Su, Eu, out_5
  BRegister bregister_1 ();  // open: n_Lo, CLK, out_4, out_3
  BinaryDisplay binarydisplay_1 ();
endmodule

module ProgramCounter (
  input  Cp,
  input  n_CLK,
  input  n_CLR,
  input  Ep,
  output [3:0] out_5
);
endmodule

module InputAndMAR (
  input  n_Lm,
  input  [3:0] in_2,
  input  CLK,
  output [3:0] out_4,
  output [3:0] out_5
);
endmodule

module RAM16x8 (
  input  [3:0] in_1,
  input  [3:0] in_2,
  input  n_CE,
  output [7:0] out_4
);
endmodule

module InstructionRegister (
  input  Li,
  input  [7:0] in_2,
  input  CLK,
  input  CLR,
  input  n_Ei,
  output [3:0] out_6,
  output [3:0] out_7
);
endmodule

module Controller (
  input  [3:0] in_1,
  output CLK,
  output nCLK,
  output CLR,
  output nCLR,
  output [11:0] out_6
);
endmodule

module AccumulatorA (
  input  n_La,
  input  [7:0] in_2,
  input  CLK,
  input  Ea,
  output [7:0] out_5,
  output [7:0] out_6
);
endmodule

module AdderSubtractor (
  input  [7:0] in_1,
  input  Su,
  input  Eu,
  input  [7:0] in_4,
  output [7:0] out_5
);
endmodule

module BRegister (
  input  n_Lo,
  input  CLK,
  output [7:0] out_3,
  output [7:0] out_4
);
endmodule
